# Fritzing sketch Hardware_with_power_sensor (saved by Fritzing 0.9.3b)
breadboards: 1

parts:
  R1 = Resistor [tolerance=±5% resistance=6.8k package=THT]
  R2 = Resistor [tolerance=±5% resistance=680 package=THT]
  Q1 = MOSFET-NCHANNEL [package=to220v]
  D1 = Rectifier Diode 10A
  WeMos_D1_Mini = WeMos D1 Mini
  C1 = Capacitor Polarized [part_number=470uF package=panasonic_e]
  VCC1 = Battery block 9V
  J1 = JST-B3P-VH [part_number=JST package=THT]
  J2 = JST-VHR-3N [part_number=JST package=THT]
  IKEA_Smoke_Sensor = mystery part, 3 pins [chip_label=CS2105G0-S12]
  U1 = V_REG_LD1117VXX [part_number=AMS1117 package=78xxl]
  R3 = Resistor [tolerance=±5% resistance=20k package=THT]
  R4 = Resistor [tolerance=±5% resistance=10k package=THT]

nets:
  N1: R1.Pin_0, R2.Pin_1, Q1.G
  N2: R1.Pin_1, Q1.S, J1.pin2
  N3: R2.Pin_0, D1.cathode
  N4: Q1.D, WeMos_D1_Mini.G, C1.-, U1.GND, R4.Pin_1
  N5: D1.anode, J1.pin1
  N6: WeMos_D1_Mini.3V3, C1.+, U1.OUT
  N7: WeMos_D1_Mini.A0, R3.Pin_1, R4.Pin_0
  N8: VCC1.-, J2.pin2, J2.pin_5, IKEA_Smoke_Sensor.pin2
  N9: VCC1.+, J2.pin3, J2.pin_6, IKEA_Smoke_Sensor.pin1
  N10: J1.pin3, U1.IN, R3.Pin_0
  N11: J2.pin1, J2.pin_4, IKEA_Smoke_Sensor.pin3
